# Fritzing sketch line-follower (saved by Fritzing 0.9.3b)
breadboards: 1

parts:
  Raspberry_Pi_2 = Raspberry Pi 3 [part_number=RPI-3-V1.2]
  IC1 = L293D [package=THT]
  M2 = DC Motor
  M1 = DC Motor
  VCC1 = 4 x AAA Battery Mount

nets:
  N1: Raspberry_Pi_2.GIPO6, IC1.In_4
  N2: Raspberry_Pi_2.GIPO13, IC1.In_3
  N3: Raspberry_Pi_2.GIPO19, IC1.Enable_2
  N4: Raspberry_Pi_2.GIPO21, IC1.Enable_1
  N5: Raspberry_Pi_2.GIPO20, IC1.In_1
  N6: Raspberry_Pi_2.GIPO16, IC1.In_2
  N7: Raspberry_Pi_2.GND, IC1.0V, VCC1.-
  N8: Raspberry_Pi_2.5V, IC1.+V, M2.pin_2
  N9: IC1.Out_1_(_Controlled_by_Enable_1_), M1.pin_2
  N10: IC1.Out_2_(_Controlled_by_Enable_1_), M1.pin_1
  N11: IC1.+Vmotor, VCC1.+
